// Logisim project GFALU.circ as structural Verilog: 5 circuits, main circuit main
module main (
  input  [3:0] in_1,
  output [3:0] out_2
);

  ROM #(.addrWidth(4), .dataWidth(4)) rom_1 (.addr(in_1), .data(out_2));
  AddSub addsub_1 ();  // open: in_1, in_2, out_3
  Mult mult_1 ();  // open: in_1, in_2, out_3
  Div div_1 ();  // open: in_1, in_2, out_3

  // Notes on the sheet:
  //   contents of rom_1 (hex, n*v repeats v):
  //   1 2 4 5 7 3 6 1
endmodule

module AddSub (
  input  [3:0] in_1,
  input  [3:0] in_2,
  output [3:0] out_3
);

  assign out_3 = in_1 ^ in_2;  // XOR_Gate xor_1, 4 bits wide
endmodule

module TwosComp (
  input  [3:0] in_1,
  output [3:0] out_2
);

  Negator #(.width(4)) negator_1 (.in(in_1), .out(out_2));
endmodule

module Mult (
  input  [3:0] in_1,
  input  [3:0] in_2,
  output [3:0] out_3
);

  wire [3:0] adder_1_out;

  Adder #(.width(4)) adder_1 (.a(in_1), .b(in_2), .out(adder_1_out));  // open: cin, cout
  assign out_3 = adder_1_out & 4'b0111;  // AND_Gate and_1, 4 bits wide
endmodule

module Div (
  input  [3:0] in_1,
  input  [3:0] in_2,
  output [3:0] out_3
);

  wire comparator_1_gt, comparator_1_lt;
  wire [3:0] multiplexer_1_out, multiplexer_2_out, subtractor_1_out;

  Multiplexer #(.enable("false"), .width(4)) multiplexer_1 (
    .in0(in_2), .in1(in_1), .out(multiplexer_1_out), .sel(comparator_1_gt));
  Comparator #(.mode("unsigned"), .width(4)) comparator_1 (
    .a(in_1), .b(in_2), .gt(comparator_1_gt), .lt(comparator_1_lt));  // open: eq
  Multiplexer #(.enable("false"), .width(4)) multiplexer_2 (
    .in0(in_2), .in1(in_1), .out(multiplexer_2_out), .sel(comparator_1_lt));
  Subtractor #(.width(4)) subtractor_1 (
    .a(multiplexer_1_out), .b(multiplexer_2_out), .out(subtractor_1_out));  // open: bin, bout
  assign out_3 = subtractor_1_out & 4'b0111;  // AND_Gate and_1, 4 bits wide
endmodule
