// Logisim project add.circ as structural Verilog: 1 circuit, main circuit add
module add (
  input  [3:0] in_1,
  input  [3:0] in_2,
  output [3:0] out_3
);

  assign out_3 = in_1 ^ in_2;  // XOR_Gate xor_1, 4 bits wide
endmodule
