// Logisim project alu.circ as structural Verilog: 5 circuits, main circuit main
module main (
  input  [3:0] in_1,
  input  [3:0] opand1,
  input  [3:0] opand2,
  input  [1:0] opcode,
  output [3:0] out_5,
  output [3:0] out_6
);

  wire [3:0] add_1_out_3, div_1_out_3, mul_1_out_3;

  ROM #(.addrWidth(4), .dataWidth(4)) rom_1 (.addr(in_1), .data(out_5));
  add add_1 (.in_1(opand1), .in_2(opand2), .out_3(add_1_out_3));
  mul mul_1 (.in_1(opand1), .in_2(opand2), .out_3(mul_1_out_3));
  div div_1 (.in_1(opand1), .in_2(opand2), .out_3(div_1_out_3));
  Multiplexer #(.enable("false"), .select(2), .width(4)) multiplexer_1 (
    .in0(add_1_out_3), .in1(mul_1_out_3), .in2(div_1_out_3), .in3(opand1), .out(out_6), .sel(opcode));

  // Notes on the sheet:
  //   contents of rom_1 (hex, n*v repeats v):
  //   1 2 4 5 7 3 6 1
endmodule

module add (
  input  [3:0] in_1,
  input  [3:0] in_2,
  output [3:0] out_3
);

  assign out_3 = in_1 ^ in_2;  // XOR_Gate xor_1, 4 bits wide
endmodule

module mul (
  input  [3:0] in_1,
  input  [3:0] in_2,
  output [3:0] out_3
);

  wire [3:0] adder_1_out;

  Adder #(.width(4)) adder_1 (.a(in_1), .b(in_2), .out(adder_1_out));  // open: cin, cout
  assign out_3 = adder_1_out & 4'b0111;  // AND_Gate and_1, 4 bits wide
endmodule

module div (
  input  [3:0] in_1,
  input  [3:0] in_2,
  output [3:0] out_3
);

  wire comparator_1_gt, comparator_1_lt;
  wire [3:0] multiplexer_1_out, multiplexer_2_out, subtractor_1_out;

  Multiplexer #(.enable("false"), .width(4)) multiplexer_1 (
    .in0(in_2), .in1(in_1), .out(multiplexer_1_out), .sel(comparator_1_gt));
  Comparator #(.mode("unsigned"), .width(4)) comparator_1 (
    .a(in_1), .b(in_2), .gt(comparator_1_gt), .lt(comparator_1_lt));  // open: eq
  Multiplexer #(.enable("false"), .width(4)) multiplexer_2 (
    .in0(in_2), .in1(in_1), .out(multiplexer_2_out), .sel(comparator_1_lt));
  Subtractor #(.width(4)) subtractor_1 (
    .a(multiplexer_1_out), .b(multiplexer_2_out), .out(subtractor_1_out));  // open: bin, bout
  assign out_3 = subtractor_1_out & 4'b0111;  // AND_Gate and_1, 4 bits wide
endmodule

module tc (
  input  [3:0] in_1,
  output [3:0] out_2
);

  Negator #(.width(4)) negator_1 (.in(in_1), .out(out_2));
endmodule
