// Logisim project twoscomp.circ as structural Verilog: 1 circuit, main circuit tc
module tc (
  input  [8:0] in_1,
  output [8:0] out_2
);

  Negator #(.width(9)) negator_1 (.in(in_1), .out(out_2));
endmodule
