// Logisim project cpu2.circ as structural Verilog: 2 circuits, main circuit main
module main (
  output [5:0] out_1,
  output [5:0] out_2,
  output out_3,
  output [5:0] out_4
);

  wire and_1_out, clock_1_out, comparator_1_lt, comparator_2_eq, counter_1_q, demultiplexer_1_out2,
       not_1_out, not_2_out, not_3_out, not_4_out, not_5_out, not_6_out;
  wire [5:0] adder_1_out, demultiplexer_2_out2, demultiplexer_3_out0, demultiplexer_3_out1, gen_1_dout,
       multiplexer_1_out, multiplexer_2_out, multiplexer_3_out, opand1_q, opand2_q, PC_q, register_1_q,
       terms_q;
  wire [14:6] ram_1_dout;

  Register #(.width(6)) register_1 (.D(adder_1_out), .en(not_1_out), .clk(clock_1_out), .Q(register_1_q));  // open: clr
  not not_1 (not_1_out, comparator_1_lt);
  Multiplexer #(.enable("false"), .width(6)) multiplexer_1 (
    .in0(register_1_q), .in1(PC_q), .out(multiplexer_1_out), .sel(comparator_1_lt));
  Adder #(.width(6)) adder_1 (.a(multiplexer_1_out), .b(6'b000001), .out(adder_1_out));  // open: cin, cout
  Button reset ();  // open: out
  Comparator #(.mode("unsigned"), .width(6)) comparator_1 (
    .a(terms_q), .b(register_1_q), .lt(comparator_1_lt));  // open: gt, eq
  Clock clock_1 (.out(clock_1_out));
  not not_2 (not_2_out, comparator_1_lt);
  Register #(.width(6)) PC (.D(multiplexer_2_out), .en(1'b1), .clk(not_3_out), .Q(PC_q));  // open: clr
  Multiplexer #(.enable("false"), .width(6)) multiplexer_2 (
    .in0(adder_1_out), .in1(6'b000001), .out(multiplexer_2_out), .sel(not_2_out));
  not not_3 (not_3_out, clock_1_out);
  Comparator #(.mode("unsigned"), .width(1)) comparator_2 (
    .a(clock_1_out), .b(1'b1), .eq(comparator_2_eq));  // open: gt, lt
  RAM #(.addrWidth(6), .dataWidth(15)) ram_1 (
    .addr(PC_q), .we(1'b0), .oe(1'b1), .clk(clock_1_out), .dout({ram_1_dout, out_2}));  // open: din
  Demultiplexer #(.enable("false"), .select(2)) demultiplexer_1 (
    .out2(demultiplexer_1_out2), .in(1'b1), .sel(ram_1_dout[13:12]));  // open: out0, out1, out3
  Demultiplexer #(.enable("false"), .select(2), .width(6)) demultiplexer_2 (
    .out2(demultiplexer_2_out2), .in(ram_1_dout[11:6]), .sel(ram_1_dout[13:12]));  // open: out0, out1, out3
  Register #(.width(6)) terms (
    .D(demultiplexer_2_out2), .en(demultiplexer_1_out2), .clk(not_4_out), .Q(terms_q));  // open: clr
  not not_4 (not_4_out, clock_1_out);
  Multiplexer #(.enable("false"), .width(6)) multiplexer_3 (
    .in0(out_2), .in1(ram_1_dout[11:6]), .out(multiplexer_3_out), .sel(counter_1_q));
  Counter #(.max('h1), .width(1)) counter_1 (
    .count(clock_1_out), .Q(counter_1_q), .up(1'b1), .clk(clock_1_out));  // open: load, D, carry, clr
  not not_5 (not_5_out, ram_1_dout[14]);
  Register #(.trigger("high"), .width(6)) opand2 (
    .D(demultiplexer_3_out0), .en(clock_1_out), .clk(clock_1_out), .Q(opand2_q));  // open: clr
  and and_1 (and_1_out, not_5_out, comparator_2_eq);
  Demultiplexer #(.enable("false"), .width(6)) demultiplexer_3 (
    .out0(demultiplexer_3_out0), .out1(demultiplexer_3_out1), .in(gen_1_dout), .sel(counter_1_q));
  gen gen_1 (
    .addr(multiplexer_3_out), .clock(clock_1_out), .opcode(ram_1_dout[13:12]), .en(ram_1_dout[14]),
    .dout(gen_1_dout), .rdy(out_3), .lol(out_1));
  Register #(.trigger("high"), .width(6)) opand1 (
    .D(demultiplexer_3_out1), .en(not_6_out), .clk(not_6_out), .Q(opand1_q));  // open: clr
  not not_6 (not_6_out, clock_1_out);
  ROM #(.addrWidth(6), .dataWidth(6)) rom_1 ();  // open: addr, data
  // alu alu_1: pin names not known; wires that end beside it: opand1_q, opand2_q, 6'b000111, and_1_out, ram_1_dout[13:12], out_4

  // Notes on the sheet:
  //   contents of rom_1 (hex, n*v repeats v):
  //   1 2 4 5 7 3 6
endmodule

module gen (
  input  [5:0] addr,
  input  clock,
  input  [1:0] opcode,
  input  en,
  output [5:0] dout,
  output rdy,
  output [5:0] lol
);

  wire and_2_out, and_3_out, and_4_out, and_5_out, comparator_1_lt, comparator_2_lt, demultiplexer_1_out1,
       demultiplexer_1_out3, multiplexer_7_out, multiplexer_8_out, not_2_out, not_3_out, xor_1_out;
  wire [0:0] bitfinder_1_found;
  wire [2:0] adder_2_out, addr_ctr_q, addr_ctr_q_2, bitfinder_1_index, index_q;
  wire [5:0] adder_1_out, adder_3_out, and_1_out, and_6_out, mask_q, multiplexer_2_out, multiplexer_3_out,
       multiplexer_4_out, multiplexer_5_out, multiplexer_6_out, not_1_out, nth_q, poly_q, register_1_q,
       shifter_1_out, shifter_2_out, shifter_3_out, subtractor_1_out, xor_2_out;

  Multiplexer #(.enable("false"), .select(2)) multiplexer_1 ();  // open: in0, in1, in2, in3, out, sel
  BitFinder #(.\type ("high1"), .width(6)) bitfinder_1 (
    .in(addr), .index(bitfinder_1_index), .found(bitfinder_1_found[0]));
  Adder #(.width(6)) adder_1 (.a(register_1_q), .b(6'b000001), .out(adder_1_out));  // open: cin, cout
  Adder #(.width(3)) adder_2 (.a(3'b001), .b(bitfinder_1_index), .out(adder_2_out));  // open: cin, cout
  Register #(.width(6)) register_1 (.D(adder_1_out), .en(1'b1), .clk(clock), .Q(register_1_q), .clr(rdy));
  Register #(.width(6)) terms (.D(shifter_1_out), .en(clock), .clk(clock), .Q(lol));  // open: clr
  Demultiplexer #(.enable("false"), .select(2)) demultiplexer_1 (
    .out1(demultiplexer_1_out1), .out2(rdy), .out3(demultiplexer_1_out3), .in(1'b1), .sel(opcode));  // open: out0
  Shifter #(.width(6)) shifter_1 (.in(6'b000001), .\dist (adder_2_out), .out(shifter_1_out));
  assign not_1_out = ~shifter_1_out;  // NOT_Gate not_1, 6 bits wide
  Register #(.width(6)) poly (.D(addr), .en(rdy), .clk(clock), .Q(poly_q));  // open: clr
  Register #(.width(6)) nth (.D(and_1_out), .en(rdy), .clk(clock), .Q(nth_q));  // open: clr
  assign and_1_out = not_1_out & {addr[4:0], bitfinder_1_found[0]};  // AND_Gate and_1, 6 bits wide
  Register #(.width(3)) index (.D(bitfinder_1_index), .en(rdy), .clk(clock), .Q(index_q));  // open: clr
  Register #(.width(6)) mask (.D(subtractor_1_out), .en(rdy), .clk(clock), .Q(mask_q));  // open: clr
  Subtractor #(.width(6)) subtractor_1 (.a(shifter_1_out), .b(6'b000001), .out(subtractor_1_out));  // open: bin, bout
  Adder #(.width(6)) adder_3 (.a({addr_ctr_q_2, addr_ctr_q}), .b(6'b000001), .out(adder_3_out));  // open: cin, cout
  Comparator #(.mode("unsigned"), .width(6)) comparator_1 (
    .a(adder_3_out), .b(lol), .lt(comparator_1_lt));  // open: gt, eq
  xor xor_1 (xor_1_out, comparator_1_lt, rdy);
  and and_2 (and_2_out, demultiplexer_1_out1, en);
  and and_3 (and_3_out, demultiplexer_1_out3, en);
  Shifter #(.shift("lr"), .width(6)) shifter_2 (.in(multiplexer_2_out), .\dist (index_q), .out(shifter_2_out));
  Comparator #(.mode("unsigned"), .width(6)) comparator_2 (
    .a({3'b000, index_q}), .b(register_1_q), .lt(comparator_2_lt));  // open: gt, eq
  and and_4 (and_4_out, clock, xor_1_out);
  Register #(.width(6)) addr_ctr (
    .D(adder_3_out), .en(xor_1_out), .clk(clock), .Q({addr_ctr_q_2, addr_ctr_q}), .clr(rdy));
  Multiplexer #(.enable("false"), .width(6)) multiplexer_2 (
    .in0(nth_q), .in1(dout), .out(multiplexer_2_out), .sel(comparator_2_lt));
  and and_5 (and_5_out, shifter_2_out[0], 1'b1);
  Shifter #(.width(6)) shifter_3 (.in(multiplexer_2_out), .\dist (3'b001), .out(shifter_3_out));
  not not_2 (not_2_out, comparator_2_lt);
  Multiplexer #(.enable("false"), .select(3), .width(6)) multiplexer_3 (
    .in0(6'b000001), .in1(6'b000010), .in2(6'b000100), .in3(6'b001000), .in4(6'b010000), .in5(6'b100000),
    .out(multiplexer_3_out), .sel(addr_ctr_q));  // open: in6, in7
  assign xor_2_out = shifter_3_out ^ nth_q;  // XOR_Gate xor_2, 6 bits wide
  Multiplexer #(.enable("false"), .width(6)) multiplexer_4 (
    .in0(shifter_3_out), .in1(xor_2_out), .out(multiplexer_4_out), .sel(and_5_out));
  assign and_6_out = mask_q & multiplexer_4_out;  // AND_Gate and_6, 6 bits wide
  not not_3 (not_3_out, and_4_out);
  Multiplexer #(.enable("false"), .width(6)) multiplexer_5 (
    .in0(and_6_out), .in1(multiplexer_3_out), .out(multiplexer_5_out), .sel(not_2_out));
  Multiplexer #(.enable("false"), .width(6)) multiplexer_6 (
    .in0(poly_q), .in1({addr_ctr_q_2, addr_ctr_q}), .out(multiplexer_6_out), .sel(and_3_out));
  Multiplexer #(.enable("false")) multiplexer_7 (.in0(1'b1), .in1(not_3_out), .out(multiplexer_7_out), .sel(and_3_out));
  Multiplexer #(.enable("false")) multiplexer_8 (
    .in0(clock), .in1(and_4_out), .out(multiplexer_8_out), .sel(and_3_out));
  RAM #(.addrWidth(6), .clearpin("true"), .dataWidth(6)) ram_1 (
    .addr(multiplexer_6_out), .we(and_4_out), .oe(multiplexer_7_out), .clk(multiplexer_8_out),
    .din(multiplexer_5_out), .dout(dout), .clr(and_2_out));
endmodule
