// Logisim project cpu3.circ as structural Verilog: 7 circuits, main circuit main
module main (
);

  wire alu_1_p4, clock_1_out, cu_1_add, cu_1_div, cu_1_gen, cu_1_init, cu_1_ld, cu_1_ldi, cu_1_mul,
       cu_1_poly, cu_1_rst, not_1_out, reset_out;
  wire [8:0] demultiplexer_1_out0, demultiplexer_1_out1, gen1_1_dout, gen1_1_size, multiplexer_1_out,
       opand1_q, opand2_q, pc_1_line;
  wire [11:0] ram_1_dout;

  Button reset (.out(reset_out));
  Clock clock_1 (.out(clock_1_out));
  RAM #(.addrWidth(9), .dataWidth(12), .\type ("nonvolatile")) ram_1 (
    .addr(pc_1_line), .we(1'b0), .oe(1'b1), .clk(clock_1_out), .dout(ram_1_dout));  // open: din
  pc pc_1 (
    .ldi(cu_1_ldi), .add(cu_1_add), .mul(cu_1_mul), .div(cu_1_div), .ld(cu_1_ld), .size(gen1_1_size),
    .rst(reset_out), .clk(clock_1_out), .line(pc_1_line));
  ROM #(.addrWidth(6), .dataWidth(6)) rom_1 ();  // open: addr, data
  cu cu_1 (
    .opcode(ram_1_dout[11:9]), .ldi(cu_1_ldi), .add(cu_1_add), .mul(cu_1_mul), .div(cu_1_div), .ld(cu_1_ld),
    .init(cu_1_init), .gen(cu_1_gen), .rst(cu_1_rst), .poly(cu_1_poly));
  gen1 gen1_1 (
    .addr(ram_1_dout[8:0]), .init(cu_1_init), .gen(cu_1_gen), .rst(cu_1_rst), .clk(clock_1_out),
    .size(gen1_1_size), .dout(gen1_1_dout));
  Multiplexer #(.enable("false"), .width(9)) multiplexer_1 (
    .in0(gen1_1_dout), .in1(ram_1_dout[8:0]), .out(multiplexer_1_out), .sel(cu_1_poly));
  Demultiplexer #(.enable("false"), .width(9)) demultiplexer_1 (
    .out0(demultiplexer_1_out0), .out1(demultiplexer_1_out1), .in(multiplexer_1_out), .sel(cu_1_ld));
  not not_1 (not_1_out, cu_1_ld);
  Register #(.trigger("high"), .width(9)) opand2 (
    .D(demultiplexer_1_out0), .en(not_1_out), .clk(clock_1_out), .Q(opand2_q));  // open: clr
  Register #(.trigger("high"), .width(9)) opand1 (
    .D(demultiplexer_1_out1), .en(cu_1_ld), .clk(clock_1_out), .Q(opand1_q));  // open: clr
  // alu alu_1: pin names not known; wires that end beside it: opand1_q, opand2_q, gen1_1_size, alu_1_p4

  // Notes on the sheet:
  //   contents of rom_1 (hex, n*v repeats v):
  //   1 2 4 5 7 3 6
endmodule

module gen2 (
  input  [8:0] addr,
  input  clk,
  input  [1:0] opcode,
  input  en,
  output [8:0] size,
  output [8:0] dout,
  output ld
);

  wire and_3_out, and_4_out, and_5_out, and_6_out, comparator_1_lt, comparator_2_lt, demultiplexer_1_out0,
       demultiplexer_1_out1, demultiplexer_1_out2, demultiplexer_1_out3, multiplexer_6_out,
       multiplexer_7_out, not_2_out, not_3_out, not_4_out, xor_1_out;
  wire [0:0] bitfinder_1_found;
  wire [2:0] addr_ctr_q;
  wire [3:0] adder_2_out, bitfinder_1_index, index_q;
  wire [5:0] addr_ctr_q_2;
  wire [8:0] adder_1_out, adder_3_out, and_1_out, and_7_out, multiplexer_1_out, multiplexer_2_out,
       multiplexer_3_out, multiplexer_4_out, multiplexer_5_out, not_1_out, nth_q, register_1_q,
       shifter_1_out, shifter_2_out, shifter_3_out, subtractor_1_out, xor_2_out;

  BitFinder #(.\type ("high1"), .width(9)) bitfinder_1 (
    .in(addr), .index(bitfinder_1_index), .found(bitfinder_1_found[0]));
  Adder #(.width(9)) adder_1 (.a(register_1_q), .b(9'h1), .out(adder_1_out));  // open: cin, cout
  Adder #(.width(4)) adder_2 (.a(4'b0001), .b(bitfinder_1_index), .out(adder_2_out));  // open: cin, cout
  Register #(.width(9)) register_1 (
    .D(adder_1_out), .en(1'b1), .clk(clk), .Q(register_1_q), .clr(demultiplexer_1_out2));
  Shifter #(.width(9)) shifter_1 (.in(9'h1), .\dist (adder_2_out), .out(shifter_1_out));
  Demultiplexer #(.enable("false"), .select(2)) demultiplexer_1 (
    .out0(demultiplexer_1_out0), .out1(demultiplexer_1_out1), .out2(demultiplexer_1_out2),
    .out3(demultiplexer_1_out3), .in(1'b1), .sel(opcode));
  assign not_1_out = ~shifter_1_out;  // NOT_Gate not_1, 9 bits wide
  assign and_1_out = not_1_out & {addr[7:0], bitfinder_1_found[0]};  // AND_Gate and_1, 9 bits wide
  Subtractor #(.width(9)) subtractor_1 (.a(shifter_1_out), .b(9'h1), .out(subtractor_1_out));  // open: bin, bout
  not not_2 (not_2_out, clk);
  Adder #(.width(9)) adder_3 (.a({addr_ctr_q_2, addr_ctr_q}), .b(9'h1), .out(adder_3_out));  // open: cin, cout
  Comparator #(.mode("unsigned"), .width(9)) comparator_1 (
    .a(adder_3_out), .b(shifter_1_out), .lt(comparator_1_lt));  // open: gt, eq
  and and_2 (ld, demultiplexer_1_out0, en);
  and and_3 (and_3_out, demultiplexer_1_out1, en);
  and and_4 (and_4_out, demultiplexer_1_out3, en);
  Register #(.width(9)) nth (.D(and_1_out), .en(demultiplexer_1_out2), .clk(not_2_out), .Q(nth_q), .clr(and_3_out));
  Register #(.width(4)) index (
    .D(bitfinder_1_index), .en(demultiplexer_1_out2), .clk(not_2_out), .Q(index_q), .clr(and_3_out));
  Register #(.width(9)) mask (
    .D(subtractor_1_out), .en(demultiplexer_1_out2), .clk(not_2_out), .Q(size), .clr(and_3_out));
  xor xor_1 (xor_1_out, comparator_1_lt, demultiplexer_1_out2);
  and and_5 (and_5_out, clk, xor_1_out);
  Register #(.width(9)) addr_ctr (
    .D(adder_3_out), .en(xor_1_out), .clk(clk), .Q({addr_ctr_q_2, addr_ctr_q}), .clr(demultiplexer_1_out2));
  Shifter #(.shift("lr"), .width(9)) shifter_2 (.in(multiplexer_2_out), .\dist (index_q), .out(shifter_2_out));
  Comparator #(.mode("unsigned"), .width(9)) comparator_2 (
    .a({{5{1'b0}}, index_q}), .b(register_1_q), .lt(comparator_2_lt));  // open: gt, eq
  Shifter #(.width(9)) shifter_3 (.in(multiplexer_2_out), .\dist (4'b0001), .out(shifter_3_out));
  assign xor_2_out = shifter_3_out ^ nth_q;  // XOR_Gate xor_2, 9 bits wide
  and and_6 (and_6_out, shifter_2_out[0], 1'b1);
  Multiplexer #(.enable("false"), .width(9)) multiplexer_1 (
    .in0(shifter_3_out), .in1(xor_2_out), .out(multiplexer_1_out), .sel(and_6_out));
  assign and_7_out = size & multiplexer_1_out;  // AND_Gate and_7, 9 bits wide
  not not_3 (not_3_out, comparator_2_lt);
  Multiplexer #(.enable("false"), .width(9)) multiplexer_2 (
    .in0(nth_q), .in1(dout), .out(multiplexer_2_out), .sel(comparator_2_lt));
  not not_4 (not_4_out, and_5_out);
  Multiplexer #(.enable("false"), .select(3), .width(9)) multiplexer_3 (
    .in0(9'h1), .in1(9'h2), .in2(9'h4), .in3(9'h8), .in4(9'h10), .in5(9'h20), .in6(9'h40), .in7(9'h80),
    .out(multiplexer_3_out), .sel(addr_ctr_q));
  Multiplexer #(.enable("false"), .width(9)) multiplexer_4 (
    .in0(and_7_out), .in1(multiplexer_3_out), .out(multiplexer_4_out), .sel(not_3_out));
  Multiplexer #(.enable("false"), .width(9)) multiplexer_5 (
    .in0(addr), .in1({addr_ctr_q_2, addr_ctr_q}), .out(multiplexer_5_out), .sel(and_4_out));
  Multiplexer #(.enable("false")) multiplexer_6 (.in0(1'b1), .in1(not_4_out), .out(multiplexer_6_out), .sel(and_4_out));
  Multiplexer #(.enable("false")) multiplexer_7 (.in0(clk), .in1(and_5_out), .out(multiplexer_7_out), .sel(and_4_out));
  RAM #(.addrWidth(9), .clearpin("true"), .dataWidth(9)) ram_1 (
    .addr(multiplexer_5_out), .we(and_5_out), .oe(multiplexer_6_out), .clk(multiplexer_7_out),
    .din(multiplexer_4_out), .dout(dout), .clr(and_3_out));

  // Notes on the sheet:
  //   00 - ld
  //   01 - rst
  //   10 - init
  //   11 - gen
  //   rst
  //   gen
endmodule

module pc2 (
  input  [8:0] size,
  input  clk,
  input  rst,
  input  log,
  input  add,
  input  mul,
  input  div,
  input  ld,
  output [8:0] line
);

  wire comparator_1_lt, counter_1_q, demultiplexer_1_out0, demultiplexer_1_out1, multiplexer_3_out,
       not_1_out, not_2_out, or_1_out, or_2_out;
  wire [8:0] adder_1_out, multiplexer_1_out, multiplexer_2_out, termctr_q;

  or or_1 (or_1_out, log, add, mul, div, ld);
  Register #(.width(9)) termctr (.D(adder_1_out), .en(not_1_out), .clk(clk), .Q(termctr_q));  // open: clr
  or or_2 (or_2_out, clk, or_1_out);
  Comparator #(.mode("unsigned"), .width(9)) comparator_1 (
    .a(size), .b(termctr_q), .lt(comparator_1_lt));  // open: gt, eq
  Multiplexer #(.enable("false"), .width(9)) multiplexer_1 (
    .in0(line), .in1(termctr_q), .out(multiplexer_1_out), .sel(not_1_out));
  Demultiplexer #(.enable("false")) demultiplexer_1 (
    .out0(demultiplexer_1_out0), .out1(demultiplexer_1_out1), .in(or_2_out), .sel(or_1_out));
  Adder #(.width(9)) adder_1 (.a(multiplexer_1_out), .b(9'h1), .out(adder_1_out));  // open: cin, cout
  not not_1 (not_1_out, comparator_1_lt);
  Multiplexer #(.enable("false"), .width(9)) multiplexer_2 (
    .in0(adder_1_out), .in1(line), .out(multiplexer_2_out), .sel(not_1_out));
  Counter #(.max('h1), .width(1)) counter_1 (
    .count(demultiplexer_1_out1), .Q(counter_1_q), .up(1'b1), .clk(clk));  // open: load, D, carry, clr
  Register #(.width(9)) pcctr (.D(multiplexer_2_out), .en(1'b1), .clk(not_2_out), .Q(line), .clr(rst));
  not not_2 (not_2_out, multiplexer_3_out);
  Multiplexer #(.enable("false")) multiplexer_3 (
    .in0(demultiplexer_1_out0), .in1(counter_1_q), .out(multiplexer_3_out), .sel(or_1_out));
endmodule

module cu2 (
  input  [2:0] opcode,
  output out_2,
  output out_3,
  output out_4,
  output out_5,
  output out_6,
  output out_7,
  output out_8,
  output out_9,
  output out_10
);

  Demultiplexer #(.enable("false"), .select(3)) demultiplexer_1 (
    .out0(out_2), .out1(out_3), .out2(out_4), .out3(out_5), .out4(out_6), .out5(out_7), .out6(out_8),
    .out7(out_9), .in(1'b1), .sel(opcode));
  or or_1 (out_10, out_5, out_4);
endmodule

module gen1 (
  input  [8:0] addr,
  input  init,
  input  gen,
  input  rst,
  input  clk,
  output [8:0] size,
  output [8:0] dout
);

  wire and_2_out, and_3_out, comparator_1_lt, comparator_2_lt, multiplexer_6_out, multiplexer_7_out,
       not_2_out, not_3_out, not_4_out, xor_1_out;
  wire [0:0] bitfinder_1_found;
  wire [2:0] addr_ctr_q;
  wire [3:0] adder_2_out, bitfinder_1_index, index_q;
  wire [5:0] addr_ctr_q_2;
  wire [8:0] adder_1_out, adder_3_out, and_1_out, and_4_out, multiplexer_1_out, multiplexer_2_out,
       multiplexer_3_out, multiplexer_4_out, multiplexer_5_out, not_1_out, nth_q, register_1_q,
       shifter_1_out, shifter_2_out, shifter_3_out, subtractor_1_out, xor_2_out;

  BitFinder #(.\type ("high1"), .width(9)) bitfinder_1 (
    .in(addr), .index(bitfinder_1_index), .found(bitfinder_1_found[0]));
  Adder #(.width(9)) adder_1 (.a(register_1_q), .b(9'h1), .out(adder_1_out));  // open: cin, cout
  Adder #(.width(4)) adder_2 (.a(4'b0001), .b(bitfinder_1_index), .out(adder_2_out));  // open: cin, cout
  Register #(.width(9)) register_1 (.D(adder_1_out), .en(1'b1), .clk(clk), .Q(register_1_q), .clr(init));
  Shifter #(.width(9)) shifter_1 (.in(9'h1), .\dist (adder_2_out), .out(shifter_1_out));
  assign not_1_out = ~shifter_1_out;  // NOT_Gate not_1, 9 bits wide
  assign and_1_out = not_1_out & {addr[7:0], bitfinder_1_found[0]};  // AND_Gate and_1, 9 bits wide
  Subtractor #(.width(9)) subtractor_1 (.a(shifter_1_out), .b(9'h1), .out(subtractor_1_out));  // open: bin, bout
  not not_2 (not_2_out, clk);
  Adder #(.width(9)) adder_3 (.a({addr_ctr_q_2, addr_ctr_q}), .b(9'h1), .out(adder_3_out));  // open: cin, cout
  Comparator #(.mode("unsigned"), .width(9)) comparator_1 (
    .a(adder_3_out), .b(shifter_1_out), .lt(comparator_1_lt));  // open: gt, eq
  Register #(.width(9)) nth (.D(and_1_out), .en(init), .clk(not_2_out), .Q(nth_q), .clr(rst));
  Register #(.width(4)) index (.D(bitfinder_1_index), .en(init), .clk(not_2_out), .Q(index_q), .clr(rst));
  Register #(.width(9)) mask (.D(subtractor_1_out), .en(init), .clk(not_2_out), .Q(size), .clr(rst));
  xor xor_1 (xor_1_out, comparator_1_lt, init);
  and and_2 (and_2_out, clk, xor_1_out);
  Register #(.width(9)) addr_ctr (
    .D(adder_3_out), .en(xor_1_out), .clk(clk), .Q({addr_ctr_q_2, addr_ctr_q}), .clr(init));
  Shifter #(.shift("lr"), .width(9)) shifter_2 (.in(multiplexer_2_out), .\dist (index_q), .out(shifter_2_out));
  Comparator #(.mode("unsigned"), .width(9)) comparator_2 (
    .a({{5{1'b0}}, index_q}), .b(register_1_q), .lt(comparator_2_lt));  // open: gt, eq
  Shifter #(.width(9)) shifter_3 (.in(multiplexer_2_out), .\dist (4'b0001), .out(shifter_3_out));
  assign xor_2_out = shifter_3_out ^ nth_q;  // XOR_Gate xor_2, 9 bits wide
  and and_3 (and_3_out, shifter_2_out[0], 1'b1);
  Multiplexer #(.enable("false"), .width(9)) multiplexer_1 (
    .in0(shifter_3_out), .in1(xor_2_out), .out(multiplexer_1_out), .sel(and_3_out));
  assign and_4_out = size & multiplexer_1_out;  // AND_Gate and_4, 9 bits wide
  not not_3 (not_3_out, comparator_2_lt);
  Multiplexer #(.enable("false"), .width(9)) multiplexer_2 (
    .in0(nth_q), .in1(dout), .out(multiplexer_2_out), .sel(comparator_2_lt));
  not not_4 (not_4_out, and_2_out);
  Multiplexer #(.enable("false"), .select(3), .width(9)) multiplexer_3 (
    .in0(9'h1), .in1(9'h2), .in2(9'h4), .in3(9'h8), .in4(9'h10), .in5(9'h20), .in6(9'h40), .in7(9'h80),
    .out(multiplexer_3_out), .sel(addr_ctr_q));
  Multiplexer #(.enable("false"), .width(9)) multiplexer_4 (
    .in0(and_4_out), .in1(multiplexer_3_out), .out(multiplexer_4_out), .sel(not_3_out));
  Multiplexer #(.enable("false"), .width(9)) multiplexer_5 (
    .in0(addr), .in1({addr_ctr_q_2, addr_ctr_q}), .out(multiplexer_5_out), .sel(gen));
  Multiplexer #(.enable("false")) multiplexer_6 (.in0(1'b1), .in1(not_4_out), .out(multiplexer_6_out), .sel(gen));
  Multiplexer #(.enable("false")) multiplexer_7 (.in0(clk), .in1(and_2_out), .out(multiplexer_7_out), .sel(gen));
  RAM #(.addrWidth(9), .clearpin("true"), .dataWidth(9)) ram_1 (
    .addr(multiplexer_5_out), .we(and_2_out), .oe(multiplexer_6_out), .clk(multiplexer_7_out),
    .din(multiplexer_4_out), .dout(dout), .clr(rst));

  // Notes on the sheet:
  //   rst
endmodule

module pc (
  input  ldi,
  input  add,
  input  mul,
  input  div,
  input  ld,
  input  [8:0] size,
  input  rst,
  input  clk,
  output [8:0] line
);

  wire comparator_1_lt, counter_1_q, demultiplexer_1_out0, demultiplexer_1_out1, multiplexer_3_out,
       not_1_out, not_2_out, or_1_out, or_2_out;
  wire [8:0] adder_1_out, multiplexer_1_out, multiplexer_2_out, termctr_q;

  or or_1 (or_1_out, ldi, add, mul, div, ld);
  Register #(.width(9)) termctr (.D(adder_1_out), .en(not_1_out), .clk(clk), .Q(termctr_q));  // open: clr
  or or_2 (or_2_out, clk, or_1_out);
  Demultiplexer #(.enable("false")) demultiplexer_1 (
    .out0(demultiplexer_1_out0), .out1(demultiplexer_1_out1), .in(or_2_out), .sel(or_1_out));
  Comparator #(.mode("unsigned"), .width(9)) comparator_1 (
    .a(size), .b(termctr_q), .lt(comparator_1_lt));  // open: gt, eq
  Multiplexer #(.enable("false"), .width(9)) multiplexer_1 (
    .in0(line), .in1(termctr_q), .out(multiplexer_1_out), .sel(not_1_out));
  Adder #(.width(9)) adder_1 (.a(multiplexer_1_out), .b(9'h1), .out(adder_1_out));  // open: cin, cout
  Counter #(.max('h1), .width(1)) counter_1 (
    .count(demultiplexer_1_out1), .Q(counter_1_q), .up(1'b1), .clk(clk));  // open: load, D, carry, clr
  not not_1 (not_1_out, comparator_1_lt);
  Multiplexer #(.enable("false"), .width(9)) multiplexer_2 (
    .in0(adder_1_out), .in1(line), .out(multiplexer_2_out), .sel(not_1_out));
  Multiplexer #(.enable("false")) multiplexer_3 (
    .in0(demultiplexer_1_out0), .in1(counter_1_q), .out(multiplexer_3_out), .sel(or_1_out));
  Register #(.width(9)) pcctr (.D(multiplexer_2_out), .en(1'b1), .clk(not_2_out), .Q(line), .clr(rst));
  not not_2 (not_2_out, multiplexer_3_out);
endmodule

module cu (
  input  [2:0] opcode,
  output ldi,
  output add,
  output mul,
  output div,
  output ld,
  output init,
  output gen,
  output rst,
  output poly
);

  wire demultiplexer_1_out4;

  Demultiplexer #(.enable("false"), .select(3)) demultiplexer_1 (
    .out0(ldi), .out1(add), .out2(mul), .out3(div), .out4(demultiplexer_1_out4), .out5(init), .out6(gen),
    .out7(rst), .in(1'b1), .sel(opcode));
  or or_1 (ld, demultiplexer_1_out4, ldi);
  or or_2 (poly, ldi, div, mul);
endmodule
