// Logisim project cu.circ as structural Verilog: 1 circuit, main circuit cu
module cu (
  input  [2:0] opcode,
  output ldi,
  output add,
  output mul,
  output div,
  output ld,
  output init,
  output gen,
  output rst,
  output elem
);

  wire demultiplexer_1_out4;

  Demultiplexer #(.enable("false"), .select(3)) demultiplexer_1 (
    .out0(ldi), .out1(add), .out2(mul), .out3(div), .out4(demultiplexer_1_out4), .out5(init), .out6(gen),
    .out7(rst), .in(1'b1), .sel(opcode));
  or or_1 (ld, demultiplexer_1_out4, ldi);
  or or_2 (elem, ldi, div, mul);
endmodule
