// Logisim project divu.circ as structural Verilog: 1 circuit, main circuit div
module div (
  input  [8:0] opand1,
  input  [8:0] opand2,
  input  [8:0] size,
  output [8:0] result
);

  wire comparator_1_gt, comparator_1_lt;
  wire [8:0] divider_1_rem, multiplexer_1_out, multiplexer_2_out, subtractor_1_out, subtractor_2_out;

  Comparator #(.mode("unsigned"), .width(9)) comparator_1 (
    .a(opand1), .b(opand2), .gt(comparator_1_gt), .lt(comparator_1_lt));  // open: eq
  Multiplexer #(.enable("false"), .width(9)) multiplexer_1 (
    .in0(opand2), .in1(opand1), .out(multiplexer_1_out), .sel(comparator_1_gt));
  Multiplexer #(.enable("false"), .width(9)) multiplexer_2 (
    .in0(opand2), .in1(opand1), .out(multiplexer_2_out), .sel(comparator_1_lt));
  Subtractor #(.width(9)) subtractor_1 (
    .a(multiplexer_1_out), .b(multiplexer_2_out), .out(subtractor_1_out));  // open: bin, bout
  Divider #(.width(9)) divider_1 (.a(subtractor_1_out), .b(size), .rem(divider_1_rem));  // open: out, upper
  Subtractor #(.width(9)) subtractor_2 (.a(size), .b(divider_1_rem), .out(subtractor_2_out));  // open: bin, bout
  Multiplexer #(.enable("false"), .width(9)) multiplexer_3 (
    .in0(divider_1_rem), .in1(subtractor_2_out), .out(result), .sel(comparator_1_lt));
endmodule
