// Logisim project gen.circ as structural Verilog: 1 circuit, main circuit main
module main (
  input  [5:0] poly,
  input  clock,
  input  [5:0] addr,
  input  en,
  output [5:0] dout,
  output rdy
);

  wire and_2_out, and_3_out, comparator_1_gt, comparator_2_lt, multiplexer_6_out, multiplexer_7_out,
       not_3_out, not_4_out;
  wire [0:0] bitfinder_1_found;
  wire [2:0] adder_2_out, addr_ctr_q, addr_ctr_q_2, bitfinder_1_index, index_q, size_q, subtractor_1_out;
  wire [5:0] adder_1_out, adder_3_out, and_1_out, and_4_out, mask_q, multiplexer_1_out, multiplexer_2_out,
       multiplexer_3_out, multiplexer_4_out, multiplexer_5_out, not_1_out, nth_q, register_1_q,
       shifter_1_out, shifter_2_out, shifter_3_out, subtractor_2_out, xor_1_out;

  BitFinder #(.\type ("high1"), .width(6)) bitfinder_1 (
    .in(poly), .index(bitfinder_1_index), .found(bitfinder_1_found[0]));
  BitFinder #(.\type ("high1")) bitfinder_2 ();  // open: in, index, found
  Adder #(.width(6)) adder_1 (.a(register_1_q), .b(6'b000001), .out(adder_1_out));  // open: cin, cout
  Adder #(.width(3)) adder_2 (.a(3'b001), .b(bitfinder_1_index), .out(adder_2_out));  // open: cin, cout
  Register #(.width(6)) register_1 (.D(adder_1_out), .en(1'b1), .clk(clock), .Q(register_1_q));  // open: clr
  Shifter #(.width(6)) shifter_1 (.in(6'b000001), .\dist (adder_2_out), .out(shifter_1_out));
  assign not_1_out = ~shifter_1_out;  // NOT_Gate not_1, 6 bits wide
  Register #(.width(6)) nth (.D(and_1_out), .en(clock), .clk(clock), .Q(nth_q));  // open: clr
  assign and_1_out = not_1_out & {poly[4:0], bitfinder_1_found[0]};  // AND_Gate and_1, 6 bits wide
  Register #(.width(3)) size (.D(adder_2_out), .en(clock), .clk(clock), .Q(size_q));  // open: clr
  Register #(.width(3)) index (.D(subtractor_1_out), .en(clock), .clk(clock), .Q(index_q));  // open: clr
  Subtractor #(.width(3)) subtractor_1 (.a(adder_2_out), .b(3'b001), .out(subtractor_1_out));  // open: bin, bout
  Register #(.width(6)) mask (.D(subtractor_2_out), .en(clock), .clk(clock), .Q(mask_q));  // open: clr
  Subtractor #(.width(6)) subtractor_2 (.a(shifter_1_out), .b(6'b000001), .out(subtractor_2_out));  // open: bin, bout
  Adder #(.width(6)) adder_3 (.a({addr_ctr_q_2, addr_ctr_q}), .b(6'b000001), .out(adder_3_out));  // open: cin, cout
  Comparator #(.mode("unsigned"), .width(6)) comparator_1 (
    .a(adder_3_out), .b(shifter_1_out), .gt(comparator_1_gt));  // open: eq, lt
  not not_2 (rdy, comparator_1_gt);
  Shifter #(.shift("lr"), .width(6)) shifter_2 (.in(multiplexer_1_out), .\dist (index_q), .out(shifter_2_out));
  Comparator #(.mode("unsigned"), .width(6)) comparator_2 (
    .a({3'b000, size_q}), .b(register_1_q), .lt(comparator_2_lt));  // open: gt, eq
  and and_2 (and_2_out, clock, rdy);
  Register #(.width(6)) addr_ctr (.D(adder_3_out), .en(rdy), .clk(clock), .Q({addr_ctr_q_2, addr_ctr_q}));  // open: clr
  Multiplexer #(.enable("false"), .width(6)) multiplexer_1 (
    .in0(nth_q), .in1(dout), .out(multiplexer_1_out), .sel(comparator_2_lt));
  and and_3 (and_3_out, 1'b1, shifter_2_out[0]);
  Shifter #(.width(6)) shifter_3 (.in(multiplexer_1_out), .\dist (3'b001), .out(shifter_3_out));
  not not_3 (not_3_out, comparator_2_lt);
  assign xor_1_out = shifter_3_out ^ nth_q;  // XOR_Gate xor_1, 6 bits wide
  Multiplexer #(.enable("false"), .width(6)) multiplexer_2 (
    .in0(shifter_3_out), .in1(xor_1_out), .out(multiplexer_2_out), .sel(and_3_out));
  assign and_4_out = mask_q & multiplexer_2_out;  // AND_Gate and_4, 6 bits wide
  Multiplexer #(.enable("false"), .select(3), .width(6)) multiplexer_3 (
    .in0({6{1'b1}}), .in1(6'b000001), .in2(6'b000010), .in3(6'b000100), .in4(6'b001000), .in5(6'b010000),
    .in6(6'b100000), .out(multiplexer_3_out), .sel(addr_ctr_q));  // open: in7
  not not_4 (not_4_out, and_2_out);
  Multiplexer #(.enable("false"), .width(6)) multiplexer_4 (
    .in0(and_4_out), .in1(multiplexer_3_out), .out(multiplexer_4_out), .sel(not_3_out));
  Multiplexer #(.enable("false"), .width(6)) multiplexer_5 (
    .in0(addr), .in1({addr_ctr_q_2, addr_ctr_q}), .out(multiplexer_5_out), .sel(en));
  Multiplexer #(.enable("false")) multiplexer_6 (.in0(1'b1), .in1(not_4_out), .out(multiplexer_6_out), .sel(en));
  Multiplexer #(.enable("false")) multiplexer_7 (.in0(clock), .in1(and_2_out), .out(multiplexer_7_out), .sel(en));
  RAM #(.addrWidth(6), .dataWidth(6)) ram_1 (
    .addr(multiplexer_5_out), .we(and_2_out), .oe(multiplexer_6_out), .clk(multiplexer_7_out),
    .din(multiplexer_4_out), .dout(dout));
endmodule
