// Logisim project mul.circ as structural Verilog: 1 circuit, main circuit mul
module mul (
  input  [5:0] opand1,
  input  [5:0] opand2,
  input  [5:0] size,
  output [5:0] result
);

  wire [5:0] adder_1_out;

  Adder #(.width(6)) adder_1 (.a(opand1), .b(opand2), .out(adder_1_out));  // open: cin, cout
  Divider #(.width(6)) divider_1 (.a(adder_1_out), .b(size), .rem(result));  // open: out, upper
endmodule
