// Logisim project pc.circ as structural Verilog: 1 circuit, main circuit pc
module pc (
  input  ldi,
  input  add,
  input  mul,
  input  div,
  input  ld,
  input  [8:0] size,
  input  rst,
  input  clk,
  output [8:0] line
);

  wire comparator_1_lt, counter_1_q, demultiplexer_1_out0, demultiplexer_1_out1, multiplexer_3_out,
       not_1_out, not_2_out, or_1_out, or_2_out;
  wire [8:0] adder_1_out, multiplexer_1_out, multiplexer_2_out, termctr_q;

  or or_1 (or_1_out, ldi, add, mul, div, ld);
  Register #(.width(9)) termctr (.D(adder_1_out), .en(not_1_out), .clk(clk), .Q(termctr_q));  // open: clr
  or or_2 (or_2_out, clk, or_1_out);
  Demultiplexer #(.enable("false")) demultiplexer_1 (
    .out0(demultiplexer_1_out0), .out1(demultiplexer_1_out1), .in(or_2_out), .sel(or_1_out));
  Comparator #(.mode("unsigned"), .width(9)) comparator_1 (
    .a(size), .b(termctr_q), .lt(comparator_1_lt));  // open: gt, eq
  Multiplexer #(.enable("false"), .width(9)) multiplexer_1 (
    .in0(line), .in1(termctr_q), .out(multiplexer_1_out), .sel(not_1_out));
  Adder #(.width(9)) adder_1 (.a(multiplexer_1_out), .b(9'h1), .out(adder_1_out));  // open: cin, cout
  Counter #(.max('h1), .width(1)) counter_1 (
    .count(demultiplexer_1_out1), .Q(counter_1_q), .up(1'b1), .clk(clk));  // open: load, D, carry, clr
  not not_1 (not_1_out, comparator_1_lt);
  Multiplexer #(.enable("false"), .width(9)) multiplexer_2 (
    .in0(adder_1_out), .in1(line), .out(multiplexer_2_out), .sel(not_1_out));
  Multiplexer #(.enable("false")) multiplexer_3 (
    .in0(demultiplexer_1_out0), .in1(counter_1_q), .out(multiplexer_3_out), .sel(or_1_out));
  Register #(.width(9)) pcctr (.D(multiplexer_2_out), .en(1'b1), .clk(not_2_out), .Q(line), .clr(rst));
  not not_2 (not_2_out, multiplexer_3_out);
endmodule
