// Logisim project polygen.circ as structural Verilog: 1 circuit, main circuit polygen
module polygen (
  input  [8:0] addr,
  input  init,
  input  gen,
  input  rst,
  input  clk,
  output [8:0] size,
  output [8:0] dout
);

  wire and_2_out, and_3_out, comparator_1_lt, comparator_2_lt, multiplexer_6_out, multiplexer_7_out,
       not_2_out, not_3_out, not_4_out, xor_1_out;
  wire [0:0] bitfinder_1_found;
  wire [2:0] addr_ctr_q;
  wire [3:0] adder_2_out, bitfinder_1_index, index_q;
  wire [5:0] addr_ctr_q_2;
  wire [8:0] adder_1_out, adder_3_out, and_1_out, and_4_out, multiplexer_1_out, multiplexer_2_out,
       multiplexer_3_out, multiplexer_4_out, multiplexer_5_out, not_1_out, nth_q, register_1_q,
       shifter_1_out, shifter_2_out, shifter_3_out, subtractor_1_out, xor_2_out;

  BitFinder #(.\type ("high1"), .width(9)) bitfinder_1 (
    .in(addr), .index(bitfinder_1_index), .found(bitfinder_1_found[0]));
  Adder #(.width(9)) adder_1 (.a(register_1_q), .b(9'h1), .out(adder_1_out));  // open: cin, cout
  Adder #(.width(4)) adder_2 (.a(4'b0001), .b(bitfinder_1_index), .out(adder_2_out));  // open: cin, cout
  Register #(.width(9)) register_1 (.D(adder_1_out), .en(1'b1), .clk(clk), .Q(register_1_q), .clr(init));
  Shifter #(.width(9)) shifter_1 (.in(9'h1), .\dist (adder_2_out), .out(shifter_1_out));
  assign not_1_out = ~shifter_1_out;  // NOT_Gate not_1, 9 bits wide
  assign and_1_out = not_1_out & {addr[7:0], bitfinder_1_found[0]};  // AND_Gate and_1, 9 bits wide
  Subtractor #(.width(9)) subtractor_1 (.a(shifter_1_out), .b(9'h1), .out(subtractor_1_out));  // open: bin, bout
  not not_2 (not_2_out, clk);
  Adder #(.width(9)) adder_3 (.a({addr_ctr_q_2, addr_ctr_q}), .b(9'h1), .out(adder_3_out));  // open: cin, cout
  Comparator #(.mode("unsigned"), .width(9)) comparator_1 (
    .a(adder_3_out), .b(shifter_1_out), .lt(comparator_1_lt));  // open: gt, eq
  Register #(.width(9)) nth (.D(and_1_out), .en(init), .clk(not_2_out), .Q(nth_q), .clr(rst));
  Register #(.width(4)) index (.D(bitfinder_1_index), .en(init), .clk(not_2_out), .Q(index_q), .clr(rst));
  Register #(.width(9)) mask (.D(subtractor_1_out), .en(init), .clk(not_2_out), .Q(size), .clr(rst));
  xor xor_1 (xor_1_out, comparator_1_lt, init);
  and and_2 (and_2_out, clk, xor_1_out);
  Register #(.width(9)) addr_ctr (
    .D(adder_3_out), .en(xor_1_out), .clk(clk), .Q({addr_ctr_q_2, addr_ctr_q}), .clr(init));
  Shifter #(.shift("lr"), .width(9)) shifter_2 (.in(multiplexer_2_out), .\dist (index_q), .out(shifter_2_out));
  Comparator #(.mode("unsigned"), .width(9)) comparator_2 (
    .a({{5{1'b0}}, index_q}), .b(register_1_q), .lt(comparator_2_lt));  // open: gt, eq
  Shifter #(.width(9)) shifter_3 (.in(multiplexer_2_out), .\dist (4'b0001), .out(shifter_3_out));
  assign xor_2_out = shifter_3_out ^ nth_q;  // XOR_Gate xor_2, 9 bits wide
  and and_3 (and_3_out, shifter_2_out[0], 1'b1);
  Multiplexer #(.enable("false"), .width(9)) multiplexer_1 (
    .in0(shifter_3_out), .in1(xor_2_out), .out(multiplexer_1_out), .sel(and_3_out));
  assign and_4_out = size & multiplexer_1_out;  // AND_Gate and_4, 9 bits wide
  not not_3 (not_3_out, comparator_2_lt);
  Multiplexer #(.enable("false"), .width(9)) multiplexer_2 (
    .in0(nth_q), .in1(dout), .out(multiplexer_2_out), .sel(comparator_2_lt));
  not not_4 (not_4_out, and_2_out);
  Multiplexer #(.enable("false"), .select(3), .width(9)) multiplexer_3 (
    .in0(9'h1), .in1(9'h2), .in2(9'h4), .in3(9'h8), .in4(9'h10), .in5(9'h20), .in6(9'h40), .in7(9'h80),
    .out(multiplexer_3_out), .sel(addr_ctr_q));
  Multiplexer #(.enable("false"), .width(9)) multiplexer_4 (
    .in0(and_4_out), .in1(multiplexer_3_out), .out(multiplexer_4_out), .sel(not_3_out));
  Multiplexer #(.enable("false"), .width(9)) multiplexer_5 (
    .in0(addr), .in1({addr_ctr_q_2, addr_ctr_q}), .out(multiplexer_5_out), .sel(gen));
  Multiplexer #(.enable("false")) multiplexer_6 (.in0(1'b1), .in1(not_4_out), .out(multiplexer_6_out), .sel(gen));
  Multiplexer #(.enable("false")) multiplexer_7 (.in0(clk), .in1(and_2_out), .out(multiplexer_7_out), .sel(gen));
  RAM #(.addrWidth(9), .clearpin("true"), .dataWidth(9)) ram_1 (
    .addr(multiplexer_5_out), .we(and_2_out), .oe(multiplexer_6_out), .clk(multiplexer_7_out),
    .din(multiplexer_4_out), .dout(dout), .clr(rst));

  // Notes on the sheet:
  //   rst
endmodule
